// Logisim project 4_bit_fisherman.circ as structural Verilog: 15 circuits, main circuit half_adder
module half_adder (
  input  A,
  input  B,
  output SUM,
  output CARRY
);

  xor xor_1 (SUM, A, B);
  and and_1 (CARRY, A, B);
endmodule

module full_adder (
  input  A,
  input  B,
  input  Cin,
  output Sum,
  output Cout
);

  wire and_1_out, and_2_out, xor_1_out;

  xor xor_1 (xor_1_out, A, B);
  and and_1 (and_1_out, A, B);
  xor xor_2 (Sum, xor_1_out, Cin);
  and and_2 (and_2_out, xor_1_out, Cin);
  or or_1 (Cout, and_2_out, and_1_out);
endmodule

module d_latch (
  input  E,
  input  D,
  output Q,
  output Qc
);

  wire and_1_out, and_2_out, not_1_out;

  not not_1 (not_1_out, D);
  and and_1 (and_1_out, not_1_out, E);
  and and_2 (and_2_out, E, D);
  nor nor_1 (Q, and_1_out, Qc);
  nor nor_2 (Qc, Q, and_2_out);
endmodule

module ALU (
  input  [3:0] A,
  input  [3:0] B,
  input  Subtract_mode,
  output [3:0] Sum,
  output Overflow
);

  wire ripple_carry_adder_1_c3, ripple_carry_adder_1_cout;
  wire [3:0] xor_1_out;

  xor xor_1 (xor_1_out[0], B[0], Subtract_mode);
  xor xor_2 (xor_1_out[1], B[1], Subtract_mode);
  xor xor_3 (xor_1_out[2], B[2], Subtract_mode);
  xor xor_4 (xor_1_out[3], B[3], Subtract_mode);
  ripple_carry_adder ripple_carry_adder_1 (
    .Cin0(Subtract_mode), .A(A), .B(xor_1_out), .Result(Sum), .Cout(ripple_carry_adder_1_cout),
    .C3(ripple_carry_adder_1_c3));
  xor xor_5 (Overflow, ripple_carry_adder_1_cout, ripple_carry_adder_1_c3);
endmodule

module ripple_carry_adder (
  input  Cin0,
  input  [3:0] A,
  input  [3:0] B,
  output [3:0] Result,
  output Cout,
  output C3
);

  wire full_adder_1_cout, full_adder_2_cout;

  full_adder full_adder_1 (.A(A[0]), .B(B[0]), .Cin(Cin0), .Sum(Result[0]), .Cout(full_adder_1_cout));
  full_adder full_adder_2 (.A(A[1]), .B(B[1]), .Cin(full_adder_1_cout), .Sum(Result[1]), .Cout(full_adder_2_cout));
  full_adder full_adder_3 (.A(A[2]), .B(B[2]), .Cin(full_adder_2_cout), .Sum(Result[2]), .Cout(C3));
  full_adder full_adder_4 (.A(A[3]), .B(B[3]), .Cin(C3), .Sum(Result[3]), .Cout(Cout));
endmodule

module main (
  input  sub,
  input  [3:0] A,
  input  [3:0] B,
  input  WE,
  input  OE
);

  wire alu_1_overflow, nand_1_out;
  wire [3:0] four_bit_memory_1_out_4, sm_mem;
  wire [6:0] decoder_7segment_4bit_1_out_2, decoder_7segment_4bit_2_out_2, decoder_7segment_4bit_3_out_2,
       decoder_7segment_4bit_4_out_2;

  decoder_7segment_4bit decoder_7segment_4bit_1 (.in_1(A), .out_2(decoder_7segment_4bit_1_out_2));
  decoder_7segment_4bit decoder_7segment_4bit_2 (.in_1(B), .out_2(decoder_7segment_4bit_2_out_2));
  LED led_1 (.in(decoder_7segment_4bit_1_out_2[5]));
  LED led_2 (.in(decoder_7segment_4bit_1_out_2[5]));
  LED led_3 (.in(decoder_7segment_4bit_1_out_2[5]));
  LED led_4 (.in(decoder_7segment_4bit_1_out_2[4]));
  LED led_5 (.in(decoder_7segment_4bit_1_out_2[4]));
  LED led_6 (.in(decoder_7segment_4bit_1_out_2[4]));
  LED led_7 (.in(decoder_7segment_4bit_1_out_2[0]));
  LED led_8 (.in(decoder_7segment_4bit_1_out_2[0]));
  LED led_9 (.in(decoder_7segment_4bit_1_out_2[0]));
  LED led_10 (.in(decoder_7segment_4bit_1_out_2[1]));
  LED led_11 (.in(decoder_7segment_4bit_1_out_2[1]));
  LED led_12 (.in(decoder_7segment_4bit_1_out_2[1]));
  LED led_13 (.in(decoder_7segment_4bit_1_out_2[6]));
  LED led_14 (.in(decoder_7segment_4bit_1_out_2[6]));
  LED led_15 (.in(decoder_7segment_4bit_1_out_2[6]));
  LED led_16 (.in(decoder_7segment_4bit_1_out_2[2]));
  LED led_17 (.in(decoder_7segment_4bit_1_out_2[2]));
  LED led_18 (.in(decoder_7segment_4bit_1_out_2[2]));
  LED led_19 (.in(decoder_7segment_4bit_1_out_2[3]));
  LED led_20 (.in(decoder_7segment_4bit_1_out_2[3]));
  LED led_21 (.in(decoder_7segment_4bit_1_out_2[3]));
  LED led_22 (.in(A[3]));
  LED led_23 (.in(A[3]));
  LED led_24 (.in(A[3]));
  LED led_25 (.in(alu_1_overflow));
  LED led_26 (.in(alu_1_overflow));
  LED led_27 (.in(alu_1_overflow));
  LED led_28 (.in(alu_1_overflow));
  LED led_29 (.in(alu_1_overflow));
  LED led_30 (.in(alu_1_overflow));
  LED led_31 (.in(alu_1_overflow));
  LED led_32 (.in(nand_1_out));
  LED led_33 (.in(nand_1_out));
  LED led_34 (.in(1'b1));
  LED led_35 (.in(1'b1));
  LED led_36 (.in(1'b1));
  LED led_37 (.in(nand_1_out));
  LED led_38 (.in(nand_1_out));
  four_bit_memory four_bit_memory_1 (.WE(WE), .D(sm_mem), .OE(OE), .out_4(four_bit_memory_1_out_4));
  decoder_7segment_4bit decoder_7segment_4bit_3 (.in_1(four_bit_memory_1_out_4), .out_2(decoder_7segment_4bit_3_out_2));
  LED led_39 (.in(alu_1_overflow));
  LED led_40 (.in(alu_1_overflow));
  LED led_41 (.in(alu_1_overflow));
  LED led_42 (.in(alu_1_overflow));
  LED led_43 (.in(alu_1_overflow));
  LED led_44 (.in(alu_1_overflow));
  LED led_45 (.in(alu_1_overflow));
  LED led_46 (.in(alu_1_overflow));
  LED led_47 (.in(alu_1_overflow));
  LED led_48 (.in(alu_1_overflow));
  LED led_49 (.in(alu_1_overflow));
  LED led_50 (.in(alu_1_overflow));
  LED led_51 (.in(1'b1));
  LED led_52 (.in(1'b1));
  ALU alu_1 (.A(A), .B(B), .Subtract_mode(sub), .Sum(sm_mem), .Overflow(alu_1_overflow));
  LED led_53 (.in(decoder_7segment_4bit_2_out_2[0]));
  LED led_54 (.in(decoder_7segment_4bit_2_out_2[0]));
  LED led_55 (.in(decoder_7segment_4bit_2_out_2[0]));
  LED led_56 (.in(decoder_7segment_4bit_2_out_2[5]));
  LED led_57 (.in(decoder_7segment_4bit_2_out_2[5]));
  LED led_58 (.in(decoder_7segment_4bit_2_out_2[5]));
  LED led_59 (.in(decoder_7segment_4bit_2_out_2[6]));
  LED led_60 (.in(decoder_7segment_4bit_2_out_2[6]));
  LED led_61 (.in(decoder_7segment_4bit_2_out_2[6]));
  LED led_62 (.in(decoder_7segment_4bit_2_out_2[4]));
  LED led_63 (.in(decoder_7segment_4bit_2_out_2[4]));
  LED led_64 (.in(decoder_7segment_4bit_2_out_2[4]));
  LED led_65 (.in(decoder_7segment_4bit_2_out_2[3]));
  LED led_66 (.in(decoder_7segment_4bit_2_out_2[3]));
  LED led_67 (.in(decoder_7segment_4bit_2_out_2[3]));
  nand nand_1 (nand_1_out, 1'b1, sub);
  LED led_68 (.in(B[3]));
  LED led_69 (.in(B[3]));
  LED led_70 (.in(four_bit_memory_1_out_4[3]));
  LED led_71 (.in(four_bit_memory_1_out_4[3]));
  LED led_72 (.in(four_bit_memory_1_out_4[3]));
  LED led_73 (.in(decoder_7segment_4bit_2_out_2[1]));
  LED led_74 (.in(decoder_7segment_4bit_2_out_2[1]));
  LED led_75 (.in(decoder_7segment_4bit_2_out_2[1]));
  LED led_76 (.in(1'b1));
  LED led_77 (.in(decoder_7segment_4bit_2_out_2[2]));
  LED led_78 (.in(1'b1));
  LED led_79 (.in(decoder_7segment_4bit_2_out_2[2]));
  LED led_80 (.in(decoder_7segment_4bit_2_out_2[2]));
  LED led_81 (.in(B[3]));
  LED led_82 (.in(decoder_7segment_4bit_3_out_2[0]));
  LED led_83 (.in(decoder_7segment_4bit_3_out_2[0]));
  LED led_84 (.in(decoder_7segment_4bit_3_out_2[5]));
  LED led_85 (.in(decoder_7segment_4bit_3_out_2[5]));
  LED led_86 (.in(decoder_7segment_4bit_3_out_2[5]));
  LED led_87 (.in(decoder_7segment_4bit_3_out_2[6]));
  LED led_88 (.in(decoder_7segment_4bit_3_out_2[6]));
  LED led_89 (.in(decoder_7segment_4bit_3_out_2[4]));
  LED led_90 (.in(decoder_7segment_4bit_3_out_2[4]));
  LED led_91 (.in(decoder_7segment_4bit_3_out_2[4]));
  LED led_92 (.in(decoder_7segment_4bit_3_out_2[3]));
  LED led_93 (.in(decoder_7segment_4bit_3_out_2[3]));
  LED led_94 (.in(1'b1));
  LED led_95 (.in(1'b1));
  LED led_96 (.in(1'b1));
  LED led_97 (.in(1'b1));
  LED led_98 (.in(1'b1));
  LED led_99 (.in(1'b1));
  LED led_100 (.in(decoder_7segment_4bit_3_out_2[0]));
  LED led_101 (.in(decoder_7segment_4bit_3_out_2[1]));
  LED led_102 (.in(decoder_7segment_4bit_3_out_2[1]));
  LED led_103 (.in(decoder_7segment_4bit_3_out_2[1]));
  LED led_104 (.in(decoder_7segment_4bit_3_out_2[6]));
  LED led_105 (.in(decoder_7segment_4bit_3_out_2[2]));
  LED led_106 (.in(decoder_7segment_4bit_3_out_2[2]));
  LED led_107 (.in(decoder_7segment_4bit_3_out_2[2]));
  LED led_108 (.in(decoder_7segment_4bit_3_out_2[3]));
  LED led_109 (.in(sm_mem[3]));
  LED led_110 (.in(sm_mem[3]));
  LED led_111 (.in(sm_mem[3]));
  decoder_7segment_4bit decoder_7segment_4bit_4 (.in_1(sm_mem), .out_2(decoder_7segment_4bit_4_out_2));
  LED led_112 (.in(decoder_7segment_4bit_4_out_2[0]));
  LED led_113 (.in(decoder_7segment_4bit_4_out_2[0]));
  LED led_114 (.in(decoder_7segment_4bit_4_out_2[5]));
  LED led_115 (.in(decoder_7segment_4bit_4_out_2[5]));
  LED led_116 (.in(decoder_7segment_4bit_4_out_2[5]));
  LED led_117 (.in(decoder_7segment_4bit_4_out_2[6]));
  LED led_118 (.in(decoder_7segment_4bit_4_out_2[6]));
  LED led_119 (.in(decoder_7segment_4bit_4_out_2[4]));
  LED led_120 (.in(decoder_7segment_4bit_4_out_2[4]));
  LED led_121 (.in(decoder_7segment_4bit_4_out_2[4]));
  LED led_122 (.in(decoder_7segment_4bit_4_out_2[3]));
  LED led_123 (.in(decoder_7segment_4bit_4_out_2[3]));
  LED led_124 (.in(decoder_7segment_4bit_4_out_2[0]));
  LED led_125 (.in(decoder_7segment_4bit_4_out_2[1]));
  LED led_126 (.in(decoder_7segment_4bit_4_out_2[1]));
  LED led_127 (.in(decoder_7segment_4bit_4_out_2[1]));
  LED led_128 (.in(decoder_7segment_4bit_4_out_2[6]));
  LED led_129 (.in(decoder_7segment_4bit_4_out_2[2]));
  LED led_130 (.in(decoder_7segment_4bit_4_out_2[2]));
  LED led_131 (.in(decoder_7segment_4bit_4_out_2[2]));
  LED led_132 (.in(decoder_7segment_4bit_4_out_2[3]));

  // Notes on the sheet:
  //   MEMORY
  //   Ini tanda minus
  //   Ini tanda minus
endmodule

module decoder_7segment_4bit (
  input  [3:0] in_1,
  output [6:0] out_2
);

  wire nor_1_out, seven_0_1_out_2, seven_1_1_out_2, seven_2_1_out_2, seven_3_1_out_2, seven_4_1_out_2,
       seven_5_1_out_2;

  seven_0 seven_0_1 (.in_1(in_1), .out_2(seven_0_1_out_2));
  seven_1 seven_1_1 (.in_1(in_1), .out_2(seven_1_1_out_2));
  seven_2 seven_2_1 (.in_1(in_1), .out_2(seven_2_1_out_2));
  seven_3 seven_3_1 (.in_1(in_1), .out_2(seven_3_1_out_2));
  seven_4 seven_4_1 (.in_1(in_1), .out_2(seven_4_1_out_2));
  seven_5 seven_5_1 (.in_1(in_1), .out_2(seven_5_1_out_2));
  seven_6 seven_6_1 (.in_1(in_1), .out_2(out_2[6]));
  nor nor_1 (nor_1_out, out_2[6], seven_5_1_out_2, seven_4_1_out_2, seven_3_1_out_2, seven_2_1_out_2, seven_1_1_out_2, seven_0_1_out_2);
  or or_1 (out_2[0], seven_0_1_out_2, nor_1_out);
  or or_2 (out_2[1], seven_1_1_out_2, nor_1_out);
  or or_3 (out_2[2], seven_2_1_out_2, nor_1_out);
  or or_4 (out_2[3], seven_3_1_out_2, nor_1_out);
  or or_5 (out_2[4], nor_1_out, seven_4_1_out_2);
  or or_6 (out_2[5], seven_5_1_out_2, nor_1_out);
endmodule

module seven_0 (
  input  [3:0] in_1,
  output out_2
);

  wire and_1_out, and_2_out, and_3_out, and_4_out, not_1_out, not_2_out, not_3_out, not_4_out;

  not not_1 (not_1_out, in_1[2]);
  not not_2 (not_2_out, in_1[0]);
  not not_3 (not_3_out, in_1[3]);
  not not_4 (not_4_out, in_1[1]);
  and and_1 (and_1_out, in_1[3], not_1_out);
  and and_2 (and_2_out, in_1[1], not_2_out);
  and and_3 (and_3_out, in_1[1], not_3_out);
  and and_4 (and_4_out, in_1[2], not_4_out, in_1[0]);
  or or_1 (out_2, and_1_out, and_2_out, and_3_out, and_4_out);
endmodule

module seven_1 (
  input  [3:0] in_1,
  output out_2
);

  wire and_1_out, and_2_out, and_3_out, and_4_out, and_5_out, and_6_out, not_1_out, not_2_out, not_3_out,
       not_4_out, not_5_out, not_6_out, not_7_out, not_8_out;

  not not_1 (not_1_out, in_1[1]);
  not not_2 (not_2_out, in_1[0]);
  not not_3 (not_3_out, in_1[1]);
  not not_4 (not_4_out, in_1[2]);
  not not_5 (not_5_out, in_1[3]);
  not not_6 (not_6_out, in_1[3]);
  not not_7 (not_7_out, in_1[2]);
  not not_8 (not_8_out, in_1[3]);
  and and_1 (and_1_out, in_1[3], in_1[2]);
  and and_2 (and_2_out, in_1[3], not_1_out);
  and and_3 (and_3_out, in_1[2], not_2_out, not_3_out);
  and and_4 (and_4_out, in_1[1], not_4_out, not_5_out);
  and and_5 (and_5_out, not_6_out, in_1[1], in_1[0]);
  and and_6 (and_6_out, in_1[0], not_7_out, not_8_out);
  or or_1 (out_2, and_1_out, and_2_out, and_3_out, and_4_out, and_5_out, and_6_out);
endmodule

module seven_3 (
  input  [3:0] in_1,
  output out_2
);

  wire and_1_out, and_2_out, and_3_out, and_4_out, not_1_out, not_2_out, not_3_out, not_4_out, not_5_out;

  not not_1 (not_1_out, in_1[0]);
  not not_2 (not_2_out, in_1[2]);
  not not_3 (not_3_out, in_1[2]);
  not not_4 (not_4_out, in_1[0]);
  not not_5 (not_5_out, in_1[1]);
  and and_1 (and_1_out, in_1[1], not_1_out);
  and and_2 (and_2_out, in_1[1], not_2_out);
  and and_3 (and_3_out, in_1[3], not_3_out, not_4_out);
  and and_4 (and_4_out, in_1[2], not_5_out, in_1[0]);
  or or_1 (out_2, and_1_out, and_2_out, and_3_out, and_4_out);
endmodule

module seven_2 (
  input  [3:0] in_1,
  output out_2
);

  wire and_1_out, and_2_out, and_3_out, not_1_out, not_2_out, not_3_out;

  not not_1 (not_1_out, in_1[3]);
  not not_2 (not_2_out, in_1[2]);
  not not_3 (not_3_out, in_1[1]);
  and and_1 (and_1_out, in_1[2], not_1_out);
  and and_2 (and_2_out, in_1[3], not_2_out);
  and and_3 (and_3_out, in_1[3], not_3_out);
  or or_1 (out_2, in_1[0], and_1_out, and_2_out, and_3_out);
endmodule

module seven_4 (
  input  [3:0] in_1,
  output out_2
);

  wire and_1_out, and_2_out, not_1_out, not_2_out, not_3_out;

  not not_1 (not_1_out, in_1[0]);
  not not_2 (not_2_out, in_1[2]);
  not not_3 (not_3_out, in_1[0]);
  and and_1 (and_1_out, in_1[1], not_1_out);
  and and_2 (and_2_out, in_1[3], not_2_out, not_3_out);
  or or_1 (out_2, and_1_out, and_2_out);
endmodule

module seven_5 (
  input  [3:0] in_1,
  output out_2
);

  wire and_1_out, and_2_out, and_3_out, and_4_out, not_1_out, not_2_out, not_3_out, not_4_out, not_5_out,
       not_6_out, not_7_out;

  not not_1 (not_1_out, in_1[3]);
  not not_2 (not_2_out, in_1[1]);
  not not_3 (not_3_out, in_1[1]);
  not not_4 (not_4_out, in_1[0]);
  not not_5 (not_5_out, in_1[2]);
  not not_6 (not_6_out, in_1[3]);
  not not_7 (not_7_out, in_1[0]);
  and and_1 (and_1_out, in_1[2], not_1_out, not_2_out);
  and and_2 (and_2_out, in_1[3], not_3_out, not_4_out);
  and and_3 (and_3_out, in_1[3], not_5_out, in_1[1]);
  and and_4 (and_4_out, in_1[2], not_6_out, not_7_out);
  or or_1 (out_2, and_1_out, and_2_out, and_3_out, and_4_out);
endmodule

module seven_6 (
  input  [3:0] in_1,
  output out_2
);

  wire and_1_out, and_2_out, and_3_out, and_4_out, not_1_out, not_2_out, not_3_out, not_4_out;

  not not_1 (not_1_out, in_1[2]);
  not not_2 (not_2_out, in_1[0]);
  not not_3 (not_3_out, in_1[1]);
  not not_4 (not_4_out, in_1[0]);
  and and_1 (and_1_out, in_1[1], not_1_out);
  and and_2 (and_2_out, in_1[3], not_2_out);
  and and_3 (and_3_out, in_1[2], not_3_out);
  and and_4 (and_4_out, in_1[2], not_4_out);
  or or_1 (out_2, and_1_out, and_2_out, and_3_out, and_4_out);
endmodule

module four_bit_memory (
  input  WE,
  input  [3:0] D,
  input  OE,
  output [3:0] out_4
);

  wire d_latch_1_q, d_latch_2_q, d_latch_3_q, d_latch_4_q;

  d_latch d_latch_1 (.E(WE), .D(D[0]), .Q(d_latch_1_q));  // open: Qc
  d_latch d_latch_2 (.E(WE), .D(D[1]), .Q(d_latch_2_q));  // open: Qc
  d_latch d_latch_3 (.E(WE), .D(D[2]), .Q(d_latch_3_q));  // open: Qc
  d_latch d_latch_4 (.E(WE), .D(D[3]), .Q(d_latch_4_q));  // open: Qc
  and and_1 (out_4[0], d_latch_1_q, OE);
  and and_2 (out_4[1], d_latch_2_q, OE);
  and and_3 (out_4[2], d_latch_3_q, OE);
  and and_4 (out_4[3], d_latch_4_q, OE);
endmodule
